# Fritzing sketch board (saved by Fritzing 0.8.7b)
circuit board: 13.7574cm x 10.2605cm
breadboards: 1

parts:
  Bauteil1 = Arduino Uno (Rev3)
  U1 = MAX485 [package=dil08]
  S1 = Pushbutton [package="[THT]"]
  S2 = Pushbutton [package="[THT]"]
  S3 = Pushbutton [package="[THT]"]
  DIN1 = DIN-5 jack (MIDI) [package=THT]
  J1 = shrouded pin header, 8 pins [form="♂ (shrouded male)"]
  LED1 = LED - 5mm [color="Red (633nm)" package="5 mm [THT]"]
  LED2 = LED - 5mm [color="Red (633nm)" package="5 mm [THT]"]
  R1 = Resistor [tolerance=±5% resistance=330 package=THT]
  R2 = Resistor [tolerance=±5% resistance=330 package=THT]
  R3 = Resistor [tolerance=±5% resistance=10k package=THT]
  R4 = Resistor [tolerance=±5% resistance=220 package=THT]
  R5 = Resistor [tolerance=±5% resistance=10k package=THT]
  R6 = Resistor [tolerance=±5% resistance=10k package=THT]
  R7 = Rotary Potentiometer (Small) [maximum_resistance=100kΩ package=THT]
  R8 = Rotary Potentiometer (Small) [maximum_resistance=100kΩ package=THT]
  R9 = Rotary Potentiometer (Small) [maximum_resistance=100kΩ package=THT]
  R10 = Resistor [tolerance=±5% resistance=120 package=THT]
  R11 = Resistor [tolerance=±5% resistance=100 package=THT]

nets:
  N1: Bauteil1.A0, R7.wiper
  N2: Bauteil1.A1, R8.wiper
  N3: Bauteil1.A2, R9.wiper
  N4: Bauteil1.D8, J1.pin8
  GND: Bauteil1.GND, U1.RE, U1.GND, S1.Pin_3, S1.Pin_4, S2.Pin_3, S2.Pin_4, S3.Pin_3, S3.Pin_4, DIN1.2, J1.pin1, LED1.cathode, LED2.cathode, R7.leg1, R8.leg1, R9.leg1, R11.Pin_0
  N5: Bauteil1.D1/TX, DIN1.5
  N6: Bauteil1.D2, S1.Pin_1, S1.Pin_2, R3.Pin_0
  N7: Bauteil1.D3_PWM, R1.Pin_1
  N8: Bauteil1.D4, S2.Pin_1, S2.Pin_2, R5.Pin_0
  N9: Bauteil1.D5_PWM, R2.Pin_1
  N10: Bauteil1.D6_PWM, U1.DI
  N11: Bauteil1.D7, S3.Pin_1, S3.Pin_2, R6.Pin_0
  5V: Bauteil1.5V, U1.DE, U1.VCC, R3.Pin_1, R4.Pin_0, R5.Pin_1, R6.Pin_1, R7.leg2, R8.leg2, R9.leg2
  N12: U1.RO, R11.Pin_1
  N13: U1.A, J1.pin4, R10.Pin_0
  N14: U1.B, J1.pin5, R10.Pin_1
  N15: DIN1.4, R4.Pin_1
  N16: LED1.anode, R1.Pin_0
  N17: LED2.anode, R2.Pin_0
